// Logisim project Computerception.circ as structural Verilog
module FullAdder (
  input  a,
  input  b,
  input  ci,
  output s,
  output co
);

  wire halfsum_1_c, halfsum_1_s, halfsum_2_c;

  HalfSum halfsum_1 (.a(a), .b(b), .s(halfsum_1_s), .c(halfsum_1_c));
  HalfSum halfsum_2 (.a(halfsum_1_s), .b(ci), .s(s), .c(halfsum_2_c));
  or or_1 (co, halfsum_2_c, halfsum_1_c);
endmodule

module HalfSum (
  input  a,
  input  b,
  output s,
  output c
);

  xor xor_1 (s, a, b);
  and and_1 (c, a, b);
endmodule

module _4_bit_Ripple_Carry_Adder (
  input  ci,
  input  b0,
  input  b1,
  input  b2,
  input  b3,
  input  a0,
  input  a1,
  input  a2,
  input  a3,
  output s0,
  output s1,
  output s2,
  output s3,
  output co
);

  wire fulladder_1_co, fulladder_2_co, fulladder_3_co;

  LED led_1 (.in(s0));
  FullAdder fulladder_1 (.a(a0), .b(b0), .ci(ci), .s(s0), .co(fulladder_1_co));
  LED led_2 (.in(s1));
  FullAdder fulladder_2 (.a(a1), .b(b1), .ci(fulladder_1_co), .s(s1), .co(fulladder_2_co));
  LED led_3 (.in(s2));
  FullAdder fulladder_3 (.a(a2), .b(b2), .ci(fulladder_2_co), .s(s2), .co(fulladder_3_co));
  FullAdder fulladder_4 (.a(a3), .b(b3), .ci(fulladder_3_co), .s(s3), .co(co));
  LED led_4 (.in(s3));
  LED led_5 (.in(co));

  // Notes on the sheet:
  //   1
  //   1
  //   1
  //   2
  //   4
  //   2
  //   4
  //   2
  //   8
  //   8
  //   4
  //   8
  //   16
endmodule

module _4_bit_wirh_splitter (
  input  [3:0] in_1,
  input  [3:0] in_2,
  input  in_3,
  output [4:0] out_4
);

  wire fulladder_2_co, fulladder_3_co, fulladder_4_co;

  FullAdder fulladder_1 (.a(in_2[3]), .b(in_1[3]), .ci(fulladder_3_co), .s(out_4[3]), .co(out_4[4]));
  FullAdder fulladder_2 (.a(in_2[1]), .b(in_1[1]), .ci(fulladder_4_co), .s(out_4[1]), .co(fulladder_2_co));
  FullAdder fulladder_3 (.a(in_2[2]), .b(in_1[2]), .ci(fulladder_2_co), .s(out_4[2]), .co(fulladder_3_co));
  FullAdder fulladder_4 (.a(in_2[0]), .b(in_1[0]), .ci(in_3), .s(out_4[0]), .co(fulladder_4_co));
endmodule

module _8_bit_adder (
  input  [7:0] in_1,
  input  [7:0] in_2,
  input  ci,
  output c0,
  output [7:0] out_5
);

  wire n4_bit_ripple_carry_adder_2_co;

  _4_bit_Ripple_Carry_Adder u_4_bit_ripple_carry_adder_1 (
    .ci(n4_bit_ripple_carry_adder_2_co), .b0(in_2[4]), .a0(in_1[4]), .b1(in_2[5]), .a1(in_1[5]),
    .b2(in_1[6]), .a2(in_2[6]), .b3(in_2[7]), .a3(in_1[7]), .s0(out_5[4]), .s1(out_5[5]), .s2(out_5[6]),
    .s3(out_5[7]), .co(c0));
  // Probe on in_1
  // Probe on in_2
  _4_bit_Ripple_Carry_Adder u_4_bit_ripple_carry_adder_2 (
    .ci(ci), .b0(in_2[0]), .a0(in_1[0]), .b1(in_2[1]), .a1(in_1[1]), .b2(in_2[2]), .a2(in_1[2]),
    .b3(in_2[3]), .a3(in_1[3]), .s0(out_5[0]), .s1(out_5[1]), .s2(out_5[2]), .s3(out_5[3]),
    .co(n4_bit_ripple_carry_adder_2_co));
  // Probe on out_5
endmodule

module _16_bit_adder (
  input  [15:0] in_1,
  input  [15:0] in_2,
  input  ci,
  output co,
  output [15:0] out_5
);

  wire n8_bit_adder_2_c0;

  // Probe on in_1
  _8_bit_adder u_8_bit_adder_1 (
    .in_1(in_2[15:8]), .in_2(in_1[15:8]), .c0(co), .ci(n8_bit_adder_2_c0), .out_5(out_5[15:8]));
  // Probe on out_5
  // Probe on in_2
  _8_bit_adder u_8_bit_adder_2 (
    .in_1(in_2[7:0]), .in_2(in_1[7:0]), .c0(n8_bit_adder_2_c0), .ci(ci), .out_5(out_5[7:0]));
endmodule

module Mux (
  input  [7:0] in_1,
  input  [7:0] in_2,
  input  [3:0] in_3,
  input  in_4,
  output [7:0] out_5
);

  wire [7:0] DivOut, MinusDivide, multiplier_3_out, MultOut, Squared, subtractor_1_out, SumOut, TimesSum;

  Multiplier multiplier_1 (.a(in_1), .b(in_2), .out(MultOut));  // open: cin, cout
  Adder adder_1 (.a(in_1), .b(in_2), .out(SumOut));  // open: cin, cout
  Divider divider_1 (.a(in_1), .b(in_2), .out(DivOut));  // open: upper, rem
  Multiplier multiplier_2 (.a(in_1), .b(in_1), .out(Squared));  // open: cin, cout
  Multiplier multiplier_3 (.a(in_1), .b(in_2), .out(multiplier_3_out));  // open: cin, cout
  Subtractor subtractor_1 (.a(in_1), .b(in_2), .out(subtractor_1_out));  // open: bin, bout
  Adder adder_2 (.a(multiplier_3_out), .b(in_2), .out(TimesSum));  // open: cin, cout
  Divider divider_2 (.a(subtractor_1_out), .b(in_2), .out(MinusDivide));  // open: upper, rem
  Multiplexer #(.select(4), .width(8)) multiplexer_1 (
    .in1(TimesSum), .in4(MultOut), .in8(MinusDivide), .in10(DivOut), .in12(Squared), .in13(SumOut),
    .out(out_5), .sel(in_3), .en(in_4));  // open: in0, in2, in3, in5, in6, in7, in9, in11, in14, in15

  // Other names for the same wires on the sheet: a[7:0] = in_1; b[7:0] = in_2
endmodule

module _32_bit_adder (
  input  [31:0] in_1,
  input  [31:0] in_2,
  input  ci,
  output co,
  output [31:0] out_5
);

  wire n16_bit_adder_2_co;

  // Probe on in_1
  _16_bit_adder u_16_bit_adder_1 (
    .in_1(in_2[31:16]), .in_2(in_1[31:16]), .out_5(out_5[31:16]), .ci(n16_bit_adder_2_co), .co(co));
  // Probe on out_5
  _16_bit_adder u_16_bit_adder_2 (
    .in_1(in_2[15:0]), .in_2(in_1[15:0]), .out_5(out_5[15:0]), .ci(ci), .co(n16_bit_adder_2_co));
  // Probe on in_2
endmodule
